# Fritzing sketch lightsaber (saved by Fritzing 1.0.6)
breadboards: 1

parts:
  U1 = Arduino Nano (Rev3.0)
  U3 = MCP4725 [package=SOT23-6]
  SP1 = SPEAKER [package=pcb_mount_speaker]
  U2 = InvenSense MPU6050

nets:
  N1: U1.D2, U2.INT
  3V3: U1.3V3, U3.VDD, U2.VCC
  VSS: U3.VSS, U3.AO, SP1.-, U2.GND, U2.AD0
  N2: U3.VOUT, SP1.+
  N3: U3.SCL, U2.SCL
  N4: U3.SDA, U2.SDA
